# Fritzing sketch PCBDesignOnly (saved by Fritzing 0.9.3b)
circuit board: 2.5cm x 5.6cm
breadboards: 1

parts:
  J1 = female pin header, 2 pins [form="♀ (female)"]
  J2 = female pin header, 2 pins [form="♀ (female)"]
  J3 = female pin header, 2 pins [form="♀ (female)"]
  J4 = female pin header, 2 pins [form="♀ (female)"]  # not connected
  J5 = female pin header, 2 pins [form="♀ (female)"]
  J6 = female pin header, 9 pins [form="♀ (female)"]

nets:
  N1: J1.pin2, J6.pin9
  N2: J2.pin2, J6.pin6
  N3: J3.pin2, J6.pin5
  N4: J5.pin2, J6.pin2

notes:
  Robert Dinh.
