# Fritzing sketch PN532_w_RPI (saved by Fritzing 0.9.3b)
circuit board: 2.5cm x 5.6cm
breadboards: 1

parts:
  PN532 = Adafruit PN532 Breakout [part_number="Adafruit #364"]
  Raspberry_Pi_1 = Raspberry Pi 3 [part_number=RPI-3-V1.2]
  J1 = female pin header, 2 pins [form="♀ (female)"]  # not connected
  J2 = female pin header, 2 pins [form="♀ (female)"]
  J3 = female pin header, 2 pins [form="♀ (female)"]  # not connected
  J4 = female pin header, 2 pins [form="♀ (female)"]  # not connected
  J5 = female pin header, 2 pins [form="♀ (female)"]  # not connected

nets:
  N1: PN532.MOSI/SDA/TX, Raspberry_Pi_1.GPIO2, J2.pin2
  VDD: PN532.VDD, Raspberry_Pi_1.3v3
  GND: PN532.GND, Raspberry_Pi_1.GND
  N2: PN532.NSS/SCL/RX, Raspberry_Pi_1.GPIO3

notes:
  Robert Dinh.

custom parts:
  Adafruit PN532 Breakout: The PN532 is the most popular NFC chip, and is what is embedded in pretty much every phone or device that does NFC. It can pretty much do it all, such as read and write to tags and cards, communicate with phones (say for payment processing), and 'act' like a NFC tag. If you want to do any sort of embedded NFC work, this is the chip you'll want to use! NFC (Near Field Communications) is a way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
